# Fritzing sketch Lab1 (saved by Fritzing 0.9.3b)
breadboards: 1

parts:
  Part1 = Arduino Uno (Rev3)
  R2 = Resistor [tolerance=±5% resistance=220 package=THT]
  LED2 = LED - 5mm [color="Red (633nm)" package="5 mm [THT]"]
  LED1 = LED - 5mm [color="Blue (430nm)" package="5 mm [THT]"]

nets:
  N1: Part1.D10_PWM/SS, LED2.anode
  N2: Part1.D12/MISO, LED1.anode
  N3: Part1.GND, R2.Pin_0
  N4: R2.Pin_1, LED2.cathode, LED1.cathode
