# Fritzing sketch Lab2 (saved by Fritzing 0.9.3b)
breadboards: 1

parts:
  Part1 = Arduino Uno (Rev3)
  LED2 = LED - 5mm [color="Red (633nm)" package="5 mm [THT]"]
  LED1 = LED - 5mm [color="Blue (430nm)" package="5 mm [THT]"]
  LED3 = smd LED [color="Green (555nm)" package="0805 [SMD]"]
  R4 = Resistor [tolerance=±5% resistance=220 package="0805 [SMD]"]
  R5 = Resistor [tolerance=±5% resistance=220 package="0805 [SMD]"]
  R6 = Resistor [tolerance=±5% resistance=220 package="0805 [SMD]"]

nets:
  N1: Part1.D9_PWM, LED1.anode
  N2: Part1.D10_PWM/SS, LED2.anode
  N3: Part1.D11_PWM/MOSI, LED3.anode
  N4: Part1.GND, R4.Pin_1, R5.Pin_1, R6.Pin_1
  N5: LED2.cathode, R5.Pin_0
  N6: LED1.cathode, R6.Pin_0
  N7: LED3.cathode, R4.Pin_0
