# Fritzing sketch Lab3 (saved by Fritzing 0.9.3b)
breadboards: 1

parts:
  Part1 = Arduino Uno (Rev3)
  LED2 = LED - 5mm [color="Red (633nm)" package="5 mm [THT]"]
  LED1 = LED - 5mm [color="Blue (430nm)" package="5 mm [THT]"]
  LED3 = smd LED [color="Green (555nm)" package="0805 [SMD]"]
  R4 = Resistor [tolerance=±5% resistance=220 package="0805 [SMD]"]
  R5 = Resistor [tolerance=±5% resistance=220 package="0805 [SMD]"]
  R7 = Resistor [tolerance=±5% resistance=220 package="0805 [SMD]"]
  U1 = POT [package=pot_alpha_rv16af-20]
  U2 = POT [package=pot_alpha_rv16af-20]  # not connected
  U3 = POT [package=pot_alpha_rv16af-20]

nets:
  N1: Part1.A0, U3.S
  N2: Part1.A1, U1.S
  N3: Part1.D9_PWM, LED3.anode
  N4: Part1.D10_PWM/SS, LED1.anode
  N5: Part1.D11_PWM/MOSI, LED2.anode
  N6: Part1.5V, U1.E, U3.E
  N7: Part1.GND, R4.Pin_1, R5.Pin_1, R7.Pin_1, U1.A, U3.A
  N8: LED2.cathode, R4.Pin_0
  N9: LED1.cathode, R7.Pin_0
  N10: LED3.cathode, R5.Pin_0
