# Fritzing sketch Lab4 (saved by Fritzing 0.9.3b)
breadboards: 1

parts:
  Part1 = Arduino Uno (Rev3)
  LED2 = LED - 5mm [color="Red (633nm)" package="5 mm [THT]"]
  R1 = Resistor [tolerance=±5% resistance=10k package="2010 [SMD]"]
  R2 = Resistor [tolerance=±5% resistance=10k package="2010 [SMD]"]
  J1 = Basic Force Sensing Resistor (FSR) [package=THT]

nets:
  N1: Part1.A0, R1.Pin_0, J1.pin_1
  N2: Part1.D11_PWM/MOSI, R2.Pin_1
  N3: Part1.5V, J1.pin_0
  N4: Part1.GND, LED2.cathode, R1.Pin_1, R2.Pin_0
