# Fritzing sketch Lab5 (saved by Fritzing 0.9.3b)
breadboards: 1

parts:
  Part1 = Arduino Uno (Rev3)
  R1 = Resistor [tolerance=±5% resistance=10k package="2010 [SMD]"]
  R2 = Resistor [tolerance=±5% resistance=10k package="2010 [SMD]"]
  J1 = Basic Force Sensing Resistor (FSR) [package=THT]
  R3 = PHOTOCELL [package=photocell-kit]
  R4 = Resistor [tolerance=±5% resistance=10k package="2010 [SMD]"]
  LED2 = LED - 5mm [color="Red (633nm)" package="5 mm [THT]"]

nets:
  N1: Part1.A0, R1.Pin_0, J1.pin_1
  N2: Part1.A1, R3.P$2, R4.Pin_0
  N3: Part1.D11_PWM/MOSI, R2.Pin_1
  N4: Part1.5V, J1.pin_0, R3.P$1
  N5: Part1.GND, R1.Pin_1, R2.Pin_0, R4.Pin_1, LED2.cathode
