# Fritzing sketch Lab6 (saved by Fritzing 0.9.3b)
breadboards: 1

parts:
  Part1 = Arduino Uno (Rev3)
  LED2 = LED - 5mm [color="Red (633nm)" package="5 mm [THT]"]
  LED1 = LED - 5mm [color="Blue (430nm)" package="5 mm [THT]"]
  LED3 = smd LED [color="Green (555nm)" package="0805 [SMD]"]
  R4 = Resistor [tolerance=±5% resistance=220 package="0805 [SMD]"]
  R5 = Resistor [tolerance=±5% resistance=220 package="0805 [SMD]"]
  R7 = Resistor [tolerance=±5% resistance=220 package="0805 [SMD]"]
  U3 = POT [package=pot_alpha_rv16af-20]
  J1 = Piezo Speaker

nets:
  N1: Part1.A0, U3.S
  N2: Part1.D9_PWM, LED2.cathode
  N3: Part1.D11_PWM/MOSI, LED3.cathode
  N4: Part1.GND, R4.Pin_1, R5.Pin_1, R7.Pin_1, U3.A, J1.pin1
  N5: Part1.D7, J1.pin2
  N6: Part1.5V, U3.E
  N7: LED2.anode, R5.Pin_0
  N8: LED1.anode, R7.Pin_0
  N9: LED3.anode, R4.Pin_0
