# Fritzing sketch Lab8 (saved by Fritzing 0.9.3b)
breadboards: 1

parts:
  Part1 = Arduino Uno (Rev3)
  U3 = POT [package=pot_alpha_rv16af-20]
  J1 = Basic Servo

nets:
  N1: Part1.A0, U3.S
  N2: Part1.D7, J1.pulse
  5V: Part1.5V, U3.E, J1.vcc
  GND: Part1.GND, J1.gnd
